// Logisim project stack_logical_normal.circ as structural Verilog: 18 circuits, main circuit main
module main (
  input  CLK,
  input  RESET,
  input  [1:0] COMMAND,
  input  [2:0] INDEX,
  input  [3:0] IO_DATA_in,
  output [3:0] IO_DATA_out
);

  stack stack_1 (
    .CLK(CLK), .RESET(RESET), .COMMAND(COMMAND), .INDEX(INDEX), .IO_DATA_in(IO_DATA_in),
    .IO_DATA_out(IO_DATA_out));
endmodule

module stack (
  input  CLK,
  input  RESET,
  input  [1:0] COMMAND,
  input  [2:0] INDEX,
  input  [3:0] IO_DATA_in,
  output [3:0] IO_DATA_out
);

  wire and_1_out, and_2_out, decode2bit_1_q0, decode2bit_1_q1, decode2bit_1_q2, rw0, transmission_1_p3;
  wire [2:0] and_3_out, diffmodulo5_1_q, minusone_1_q, omod, plusone_1_q, pointer, pointert_1_q, pointert_2_q;
  wire [2:2] decode2bit_1_q3;
  wire [3:0] ODATA;

  // Transmission_Gate #(.width(4)) transmission_1: pin names not known; wires that end beside it: ODATA, rw0, transmission_1_p3, IO_DATA_in, omod
  not not_1 (transmission_1_p3, rw0);
  decode2bit decode2bit_1 (
    .A(COMMAND), .Q0(decode2bit_1_q0), .Q1(decode2bit_1_q1), .Q2(decode2bit_1_q2), .Q3(decode2bit_1_q3[2]));
  plusOne plusone_1 (.A(omod), .Q(plusone_1_q));
  mod5forInd mod5forind_1 (.A(INDEX), .Q(omod));
  and and_1 (and_1_out, decode2bit_1_q1, CLK);
  and and_2 (and_2_out, decode2bit_1_q2, CLK);
  or or_1 (rw0, decode2bit_1_q1, decode2bit_1_q0);
  assign and_3_out = {3{decode2bit_1_q3[2]}} & plusone_1_q;  // AND_Gate and_3, 3 bits wide
  pointerT pointert_1 (.Reset(RESET), .CLK(and_1_out), .Q(pointert_1_q));
  pointerT pointert_2 (.Reset(RESET), .CLK(and_2_out), .Q(pointert_2_q));
  diffModulo5 diffmodulo5_1 (.A(pointer), .B(and_3_out), .Q(diffmodulo5_1_q));
  minusOne minusone_1 (.CLK(decode2bit_1_q2), .A(diffmodulo5_1_q), .Q(minusone_1_q));
  diffModulo5 diffmodulo5_2 (.A(pointert_1_q), .B(pointert_2_q), .Q(pointer));
  StackMemory stackmemory_1 (
    .CLK(CLK), .Reset(RESET), .rw(decode2bit_1_q1), .data(IO_DATA_in), .index(minusone_1_q), .Q(ODATA));

  assign IO_DATA_out = IO_DATA_in;

  // Other names for the same wires on the sheet: idata[3:0] = IO_DATA_in; tmod[2:0] = INDEX

  // Notes on the sheet:
  //   your circuit must be here
endmodule

module pointerT (
  input  Reset,
  input  CLK,
  output [2:0] Q
);

  wire and_1_out, not_1_out, or_1_out;

  or or_1 (or_1_out, and_1_out, Reset);
  Ttrigger ttrigger_1 (.Reset(or_1_out), .CLK(Q[1]), .Q(Q[2]));
  Ttrigger ttrigger_2 (.Reset(or_1_out), .CLK(Q[0]), .Q(Q[1]));
  Ttrigger ttrigger_3 (.Reset(or_1_out), .CLK(CLK), .Q(Q[0]));
  not not_1 (not_1_out, Q[1]);
  and and_1 (and_1_out, Q[2], not_1_out, Q[0]);
endmodule

module RS (
  input  Reset,
  input  R,
  input  CLK,
  input  S,
  output Q,
  output notQ
);

  wire and_1_out, and_2_out, nor_2_out;

  and and_1 (and_1_out, R, CLK);
  and and_2 (and_2_out, CLK, S);
  nor nor_1 (Q, and_1_out, notQ);
  nor nor_2 (nor_2_out, Q, and_2_out);
  or or_1 (notQ, Reset, nor_2_out);
endmodule

module Dtrigger (
  input  Reset,
  input  CLK,
  input  D,
  output Q,
  output notQ
);

  wire not_1_out;

  not not_1 (not_1_out, D);
  RS rs_1 (.Reset(Reset), .R(not_1_out), .CLK(CLK), .S(D), .Q(Q), .notQ(notQ));
endmodule

module DynamicD (
  input  Reset,
  input  CLK,
  input  D,
  output Q,
  output notQ
);

  wire dtrigger_1_q, not_1_out;

  not not_1 (not_1_out, CLK);
  Dtrigger dtrigger_1 (.Reset(Reset), .CLK(CLK), .D(D), .Q(dtrigger_1_q));  // open: notQ
  Dtrigger dtrigger_2 (.Reset(Reset), .CLK(not_1_out), .D(dtrigger_1_q), .Q(Q), .notQ(notQ));
endmodule

module Ttrigger (
  input  Reset,
  input  CLK,
  output Q
);

  wire dynamicd_1_notq;

  DynamicD dynamicd_1 (.Reset(Reset), .CLK(CLK), .D(dynamicd_1_notq), .Q(Q), .notQ(dynamicd_1_notq));
endmodule

module Memory (
  input  reset,
  input  CLK,
  input  rw,
  input  [3:0] data,
  output [3:0] Q
);

  wire and_1_out;
  wire [3:0] dtrigger_1_q;

  and and_1 (and_1_out, CLK, rw);
  Dtrigger dtrigger_1 (.Reset(reset), .CLK(and_1_out), .D(data[0]), .Q(dtrigger_1_q[0]));  // open: notQ
  Dtrigger dtrigger_2 (.Reset(reset), .CLK(and_1_out), .D(data[1]), .Q(dtrigger_1_q[1]));  // open: notQ
  Dtrigger dtrigger_3 (.Reset(reset), .CLK(and_1_out), .D(data[2]), .Q(dtrigger_1_q[2]));  // open: notQ
  Dtrigger dtrigger_4 (.Reset(reset), .CLK(and_1_out), .D(data[3]), .Q(dtrigger_1_q[3]));  // open: notQ
  assign Q = {4{CLK}} & dtrigger_1_q;  // AND_Gate and_2, 4 bits wide
endmodule

module StackMemory (
  input  CLK,
  input  Reset,
  input  rw,
  input  [3:0] data,
  input  [2:0] index,
  output [3:0] Q
);

  wire and_1_out, and_2_out, and_3_out, and_4_out, and_5_out, and_6_out, decode3bit_1_q0, decode3bit_1_q1,
       decode3bit_1_q2, decode3bit_1_q3, decode3bit_1_q4;
  wire [3:0] and_7_out, and_8_out, and_9_out, and_10_out, and_11_out, bitto4_1_q, bitto4_2_q, bitto4_3_q,
       bitto4_4_q, bitto4_5_q, memory_1_q, memory_2_q, memory_3_q, memory_4_q, memory_5_q;

  decode3bit decode3bit_1 (
    .A(index), .Q0(decode3bit_1_q0), .Q1(decode3bit_1_q1), .Q2(decode3bit_1_q2), .Q3(decode3bit_1_q3),
    .Q4(decode3bit_1_q4));
  and and_1 (and_1_out, CLK, rw);
  and and_2 (and_2_out, decode3bit_1_q0, CLK);
  and and_3 (and_3_out, decode3bit_1_q1, CLK);
  and and_4 (and_4_out, decode3bit_1_q2, CLK);
  and and_5 (and_5_out, decode3bit_1_q3, CLK);
  and and_6 (and_6_out, decode3bit_1_q4, CLK);
  Memory memory_1 (.reset(Reset), .CLK(and_2_out), .rw(and_1_out), .data(data), .Q(memory_1_q));
  Memory memory_2 (.reset(Reset), .CLK(and_3_out), .rw(and_1_out), .data(data), .Q(memory_2_q));
  Memory memory_3 (.reset(Reset), .CLK(and_4_out), .rw(and_1_out), .data(data), .Q(memory_3_q));
  Memory memory_4 (.reset(Reset), .CLK(and_5_out), .rw(and_1_out), .data(data), .Q(memory_4_q));
  Memory memory_5 (.reset(Reset), .CLK(and_6_out), .rw(and_1_out), .data(data), .Q(memory_5_q));
  bitTo4 bitto4_1 (.A(decode3bit_1_q0), .Q(bitto4_1_q));
  bitTo4 bitto4_2 (.A(decode3bit_1_q1), .Q(bitto4_2_q));
  bitTo4 bitto4_3 (.A(decode3bit_1_q2), .Q(bitto4_3_q));
  bitTo4 bitto4_4 (.A(decode3bit_1_q3), .Q(bitto4_4_q));
  bitTo4 bitto4_5 (.A(decode3bit_1_q4), .Q(bitto4_5_q));
  assign and_7_out = memory_1_q & bitto4_1_q;  // AND_Gate and_7, 4 bits wide
  assign and_8_out = memory_2_q & bitto4_2_q;  // AND_Gate and_8, 4 bits wide
  assign Q = and_7_out | and_8_out | and_9_out | and_10_out | and_11_out;  // OR_Gate or_1, 4 bits wide
  assign and_9_out = memory_3_q & bitto4_3_q;  // AND_Gate and_9, 4 bits wide
  assign and_10_out = memory_4_q & bitto4_4_q;  // AND_Gate and_10, 4 bits wide
  assign and_11_out = memory_5_q & bitto4_5_q;  // AND_Gate and_11, 4 bits wide
endmodule

module decode2bit (
  input  [1:0] A,
  output Q0,
  output Q1,
  output Q2,
  output Q3
);

  wire not_1_out, not_2_out, not_3_out, not_4_out;

  not not_1 (not_1_out, A[1]);
  not not_2 (not_2_out, A[0]);
  not not_3 (not_3_out, A[1]);
  not not_4 (not_4_out, A[0]);
  and and_1 (Q0, not_1_out, not_2_out);
  and and_2 (Q1, not_3_out, A[0]);
  and and_3 (Q2, A[1], not_4_out);
  and and_4 (Q3, A[1], A[0]);
endmodule

module decode3bit (
  input  [2:0] A,
  output Q0,
  output Q1,
  output Q2,
  output Q3,
  output Q4
);

  wire and_1_out, and_2_out, and_3_out, and_6_out, and_7_out, and_8_out, not_1_out, not_2_out, not_3_out,
       not_4_out, not_5_out, not_6_out, not_7_out, not_8_out, not_9_out, not_10_out, not_11_out, not_12_out;

  not not_1 (not_1_out, A[2]);
  not not_2 (not_2_out, A[1]);
  not not_3 (not_3_out, A[0]);
  not not_4 (not_4_out, A[2]);
  not not_5 (not_5_out, A[1]);
  not not_6 (not_6_out, A[2]);
  not not_7 (not_7_out, A[0]);
  not not_8 (not_8_out, A[2]);
  not not_9 (not_9_out, A[1]);
  not not_10 (not_10_out, A[0]);
  not not_11 (not_11_out, A[1]);
  not not_12 (not_12_out, A[0]);
  and and_1 (and_1_out, not_1_out, not_2_out, not_3_out);
  and and_2 (and_2_out, not_4_out, not_5_out, A[0]);
  and and_3 (and_3_out, not_6_out, A[1], not_7_out);
  and and_4 (Q3, not_8_out, A[1], A[0]);
  and and_5 (Q4, A[2], not_9_out, not_10_out);
  and and_6 (and_6_out, A[2], not_11_out, A[0]);
  and and_7 (and_7_out, A[2], A[1], not_12_out);
  and and_8 (and_8_out, A[2], A[1], A[0]);
  or or_1 (Q0, and_1_out, and_6_out);
  or or_2 (Q1, and_2_out, and_7_out);
  or or_3 (Q2, and_3_out, and_8_out);
endmodule

module encode3bit (
  input  A0,
  input  A1,
  input  A2,
  input  A3,
  input  A4,
  output [2:0] Q
);

  or or_1 (Q[0], A1, A3);
  or or_2 (Q[1], A2, A3);

  assign Q[2] = A4;
endmodule

module mod5forInd (
  input  [2:0] A,
  output [2:0] Q
);

  wire decode3bit_1_q0, decode3bit_1_q1, decode3bit_1_q2, decode3bit_1_q3, decode3bit_1_q4;

  decode3bit decode3bit_1 (
    .A(A), .Q0(decode3bit_1_q0), .Q1(decode3bit_1_q1), .Q2(decode3bit_1_q2), .Q3(decode3bit_1_q3),
    .Q4(decode3bit_1_q4));
  encode3bit encode3bit_1 (
    .A0(decode3bit_1_q0), .A1(decode3bit_1_q1), .A2(decode3bit_1_q2), .A3(decode3bit_1_q3),
    .A4(decode3bit_1_q4), .Q(Q));
endmodule

module bitTo4 (
  input  A,
  output [3:0] Q
);


  assign Q = {4{A}};
endmodule

module diffModulo5 (
  input  [2:0] A,
  input  [2:0] B,
  output [2:0] Q
);

  wire and_1_out, and_2_out, and_3_out, and_4_out, and_5_out, and_6_out, and_7_out, and_8_out, and_9_out,
       and_10_out, and_11_out, and_12_out, and_13_out, and_14_out, and_15_out, and_16_out, and_17_out,
       and_18_out, and_19_out, and_20_out, and_21_out, and_22_out, and_23_out, and_24_out, and_25_out,
       decode3bit_1_q0, decode3bit_1_q1, decode3bit_1_q2, decode3bit_1_q3, decode3bit_1_q4, decode3bit_2_q0,
       decode3bit_2_q1, decode3bit_2_q2, decode3bit_2_q3, decode3bit_2_q4, or_1_out, or_2_out, or_3_out,
       or_4_out, or_5_out;

  decode3bit decode3bit_1 (
    .A(B), .Q0(decode3bit_1_q0), .Q1(decode3bit_1_q1), .Q2(decode3bit_1_q2), .Q3(decode3bit_1_q3),
    .Q4(decode3bit_1_q4));
  decode3bit decode3bit_2 (
    .A(A), .Q0(decode3bit_2_q0), .Q1(decode3bit_2_q1), .Q2(decode3bit_2_q2), .Q3(decode3bit_2_q3),
    .Q4(decode3bit_2_q4));
  and and_1 (and_1_out, decode3bit_2_q0, decode3bit_1_q0);
  and and_2 (and_2_out, decode3bit_2_q1, decode3bit_1_q1);
  and and_3 (and_3_out, decode3bit_2_q2, decode3bit_1_q2);
  and and_4 (and_4_out, decode3bit_2_q3, decode3bit_1_q3);
  and and_5 (and_5_out, decode3bit_2_q4, decode3bit_1_q4);
  and and_6 (and_6_out, decode3bit_2_q0, decode3bit_1_q4);
  and and_7 (and_7_out, decode3bit_2_q1, decode3bit_1_q0);
  and and_8 (and_8_out, decode3bit_2_q2, decode3bit_1_q1);
  and and_9 (and_9_out, decode3bit_2_q3, decode3bit_1_q2);
  and and_10 (and_10_out, decode3bit_2_q4, decode3bit_1_q3);
  and and_11 (and_11_out, decode3bit_2_q0, decode3bit_1_q3);
  and and_12 (and_12_out, decode3bit_2_q1, decode3bit_1_q4);
  and and_13 (and_13_out, decode3bit_2_q2, decode3bit_1_q0);
  and and_14 (and_14_out, decode3bit_2_q3, decode3bit_1_q1);
  and and_15 (and_15_out, decode3bit_2_q4, decode3bit_1_q2);
  and and_16 (and_16_out, decode3bit_2_q0, decode3bit_1_q2);
  and and_17 (and_17_out, decode3bit_2_q1, decode3bit_1_q3);
  and and_18 (and_18_out, decode3bit_2_q2, decode3bit_1_q4);
  and and_19 (and_19_out, decode3bit_2_q3, decode3bit_1_q0);
  and and_20 (and_20_out, decode3bit_2_q4, decode3bit_1_q1);
  and and_21 (and_21_out, decode3bit_2_q0, decode3bit_1_q1);
  and and_22 (and_22_out, decode3bit_2_q1, decode3bit_1_q2);
  and and_23 (and_23_out, decode3bit_2_q2, decode3bit_1_q3);
  and and_24 (and_24_out, decode3bit_2_q3, decode3bit_1_q4);
  and and_25 (and_25_out, decode3bit_2_q4, decode3bit_1_q0);
  or or_1 (or_1_out, and_1_out, and_2_out, and_3_out, and_4_out, and_5_out);
  or or_2 (or_2_out, and_6_out, and_7_out, and_8_out, and_9_out, and_10_out);
  or or_3 (or_3_out, and_11_out, and_12_out, and_13_out, and_14_out, and_15_out);
  or or_4 (or_4_out, and_16_out, and_17_out, and_18_out, and_19_out, and_20_out);
  or or_5 (or_5_out, and_21_out, and_22_out, and_23_out, and_24_out, and_25_out);
  encode3bit encode3bit_1 (.A0(or_1_out), .A1(or_2_out), .A2(or_3_out), .A3(or_4_out), .A4(or_5_out), .Q(Q));
endmodule

module ifThenAelseB (
  input  condition,
  input  [2:0] A,
  input  [2:0] B,
  output [2:0] Q
);

  wire [2:0] and_1_out, and_2_out, not_1_out;

  assign not_1_out = ~{3{condition}};  // NOT_Gate not_1, 3 bits wide
  assign and_1_out = {3{condition}} & A;  // AND_Gate and_1, 3 bits wide
  assign Q = and_1_out | and_2_out;  // OR_Gate or_1, 3 bits wide
  assign and_2_out = not_1_out & B;  // AND_Gate and_2, 3 bits wide
endmodule

module plusOne (
  input  [2:0] A,
  output [2:0] Q
);

  wire decode3bit_1_q0, decode3bit_1_q1, decode3bit_1_q2, decode3bit_1_q3, decode3bit_1_q4;

  decode3bit decode3bit_1 (
    .A(A), .Q0(decode3bit_1_q0), .Q1(decode3bit_1_q1), .Q2(decode3bit_1_q2), .Q3(decode3bit_1_q3),
    .Q4(decode3bit_1_q4));
  encode3bit encode3bit_1 (
    .A0(decode3bit_1_q4), .A1(decode3bit_1_q0), .A2(decode3bit_1_q1), .A3(decode3bit_1_q2),
    .A4(decode3bit_1_q3), .Q(Q));
endmodule

module minusOne (
  input  CLK,
  input  [2:0] A,
  output [2:0] Q
);

  wire decode3bit_1_q0, decode3bit_1_q1, decode3bit_1_q2, decode3bit_1_q3, decode3bit_1_q4;
  wire [2:0] and_1_out, and_2_out, encode3bit_1_q;
  wire [2:2] not_1_out;

  not not_1 (not_1_out[2], CLK);
  assign and_1_out = A & {3{not_1_out[2]}};  // AND_Gate and_1, 3 bits wide
  decode3bit decode3bit_1 (
    .A(A), .Q0(decode3bit_1_q0), .Q1(decode3bit_1_q1), .Q2(decode3bit_1_q2), .Q3(decode3bit_1_q3),
    .Q4(decode3bit_1_q4));
  encode3bit encode3bit_1 (
    .A0(decode3bit_1_q1), .A1(decode3bit_1_q2), .A2(decode3bit_1_q3), .A3(decode3bit_1_q4),
    .A4(decode3bit_1_q0), .Q(encode3bit_1_q));
  assign Q = and_1_out | and_2_out;  // OR_Gate or_1, 3 bits wide
  assign and_2_out = {3{CLK}} & encode3bit_1_q;  // AND_Gate and_2, 3 bits wide
endmodule
